# Fritzing sketch HW2_Elevator_Fritz (saved by Fritzing 0.9.3b)
breadboards: 2

parts:
  Part1 = Arduino Uno (Rev3)
  S1 = Pushbutton [package="[THT]"]
  S2 = Pushbutton [package="[THT]"]
  S3 = Pushbutton [package="[THT]"]
  LED1 = LED - 5mm [color="Red (633nm)" package="5 mm [THT]"]
  LED2 = LED - 5mm [color="Red (633nm)" package="5 mm [THT]"]
  LED3 = LED - 5mm [color="Red (633nm)" package="5 mm [THT]"]
  LED4 = LED - 5mm [color="Red (633nm)" package="5 mm [THT]"]
  R1 = Resistor [tolerance=±5% resistance=220 package=THT]
  R2 = Resistor [tolerance=±5% resistance=220 package=THT]
  R3 = Resistor [tolerance=±5% resistance=220 package=THT]
  R4 = Resistor [tolerance=±5% resistance=220 package=THT]
  J1 = Piezo Speaker
  R5 = Resistor [tolerance=±5% resistance=100 package=THT]
  S4 = Pushbutton [package="[THT]"]
  LED5 = LED - 5mm [color="Red (633nm)" package="5 mm [THT]"]
  R6 = Resistor [tolerance=±5% resistance=220 package=THT]
  S5 = Pushbutton [package="[THT]"]
  LED6 = LED - 5mm [color="Red (633nm)" package="5 mm [THT]"]
  R7 = Resistor [tolerance=±5% resistance=220 package=THT]

nets:
  N1: Part1.D8, R6.Pin_0
  N2: Part1.D9_PWM, R5.Pin_1
  N3: Part1.D10_PWM/SS, R3.Pin_0
  N4: Part1.D11_PWM/MOSI, R2.Pin_0
  N5: Part1.D12/MISO, R1.Pin_0
  N6: Part1.D13/SCK, R7.Pin_0
  N7: Part1.D2, S1.Pin_1, S1.Pin_2
  N8: Part1.D3_PWM, S2.Pin_1, S2.Pin_2
  N9: Part1.D4, S3.Pin_1, S3.Pin_2
  N10: Part1.D5_PWM, S4.Pin_1, S4.Pin_2
  N11: Part1.D6_PWM, S5.Pin_1, S5.Pin_2
  N12: Part1.D7, R4.Pin_1
  N13: Part1.GND, S1.Pin_3, S1.Pin_4, S2.Pin_3, S2.Pin_4, S3.Pin_3, S3.Pin_4, LED1.cathode, LED2.cathode, LED3.cathode, LED4.cathode, J1.pin1, S4.Pin_3, S4.Pin_4, LED5.cathode, S5.Pin_3, S5.Pin_4, LED6.cathode
  N14: LED1.anode, R3.Pin_1
  N15: LED2.anode, R2.Pin_1
  N16: LED3.anode, R1.Pin_1
  N17: LED4.anode, R4.Pin_0
  N18: J1.pin2, R5.Pin_0
  N19: LED5.anode, R6.Pin_1
  N20: LED6.anode, R7.Pin_1
