# Fritzing sketch HW3_7SD_Fritz (saved by Fritzing 0.9.3b)
breadboards: 1

parts:
  DI1 = 7-Segment LED Display [package=THT]
  Part1 = Thumb Joystick
  Part2 = Arduino Uno (Rev3)
  R1 = Resistor [tolerance=±5% resistance=220 package=THT]
  R2 = Resistor [tolerance=±5% resistance=220 package=THT]
  R3 = Resistor [tolerance=±5% resistance=220 package=THT]
  R4 = Resistor [tolerance=±5% resistance=220 package=THT]
  R5 = Resistor [tolerance=±5% resistance=220 package=THT]
  R6 = Resistor [tolerance=±5% resistance=220 package=THT]
  R7 = Resistor [tolerance=±5% resistance=220 package=THT]
  R8 = Resistor [tolerance=±5% resistance=220 package=THT]

nets:
  N1: DI1.cathodeE, R8.Pin_1
  N2: DI1.cathodeD, R7.Pin_1
  VCC: DI1.commAnode, Part1.VCC, Part2.5V
  N3: DI1.cathodeC, R5.Pin_0
  N4: DI1.cathodeDP, R6.Pin_0
  N5: DI1.cathodeB, R4.Pin_0
  N6: DI1.cathodeA, R3.Pin_0
  N7: DI1.cathodeF, R2.Pin_1
  N8: DI1.cathodeG, R1.Pin_1
  GND: Part1.GND, Part2.GND
  N9: Part1.SEL, Part2.D2
  N10: Part1.HORZ, Part2.A0
  N11: Part1.VERT, Part2.A1
  N12: Part2.D8, R7.Pin_0
  N13: Part2.D9_PWM, R5.Pin_1
  N14: Part2.D10_PWM/SS, R4.Pin_1
  N15: Part2.D12/MISO, R3.Pin_1
  N16: Part2.D4, R6.Pin_1
  N17: Part2.D5_PWM, R2.Pin_0
  N18: Part2.D6_PWM, R1.Pin_0
  N19: Part2.D7, R8.Pin_0
