# Fritzing sketch HW4_Stopwatch_Fritz (saved by Fritzing 0.9.3b)
breadboards: 1

parts:
  Part1 = Arduino Uno (Rev3)
  U1 = 74HC595 SMD [package="SO16 [SMD]"]
  LED3 = 7-SEGMENT-4DIGIT-YOUNGSUN [package=7-segment-4digit-youngsun]
  R1 = Resistor [tolerance=±5% resistance=220 package=THT]
  R2 = Resistor [tolerance=±5% resistance=220 package=THT]
  R3 = Resistor [tolerance=±5% resistance=220 package=THT]
  R4 = Resistor [tolerance=±5% resistance=220 package=THT]
  R5 = Resistor [tolerance=±5% resistance=220 package=THT]
  R6 = Resistor [tolerance=±5% resistance=220 package=THT]
  R7 = Resistor [tolerance=±5% resistance=220 package=THT]
  R8 = Resistor [tolerance=±5% resistance=220 package=THT]
  S2 = Pushbutton [package="[THT]"]
  S3 = Pushbutton [package="[THT]"]
  S4 = Pushbutton [package="[THT]"]
  IR1 = TSOP312.., 314.. [package=THT]

nets:
  N1: Part1.D8, IR1.Data
  N2: Part1.D9_PWM, S3.Pin_3, S3.Pin_4
  N3: Part1.D10_PWM/SS, U1.SH_CP
  N4: Part1.D11_PWM/MOSI, U1.ST_CP
  N5: Part1.D12/MISO, U1.DS
  N6: Part1.D2, S4.Pin_3, S4.Pin_4
  N7: Part1.D3_PWM, S2.Pin_3, S2.Pin_4
  N8: Part1.D4, LED3.B
  N9: Part1.D5_PWM, LED3.C
  N10: Part1.D6_PWM, LED3.COL-C
  N11: Part1.D7, LED3.DIG3
  5V: Part1.5V, U1.MR, U1.VCC, IR1.Vs
  GND: Part1.GND, U1.GND, U1.OE, S2.Pin_1, S2.Pin_2, S3.Pin_1, S3.Pin_2, S4.Pin_1, S4.Pin_2, IR1.GND
  N12: U1.Q1, R5.Pin_1
  N13: U1.Q2, R6.Pin_0
  N14: U1.Q3, R1.Pin_0
  N15: U1.Q4, R2.Pin_0
  N16: U1.Q5, R4.Pin_1
  N17: U1.Q6, R8.Pin_1
  N18: U1.Q7, R7.Pin_0
  N19: U1.Q0, R3.Pin_0
  N20: LED3.DIG1, R1.Pin_1
  N21: LED3.DIG2, R2.Pin_1
  N22: LED3.D, R3.Pin_1
  N23: LED3.COL-A, R4.Pin_0
  N24: LED3.E, R5.Pin_0
  N25: LED3.F, R8.Pin_0
  N26: LED3.A, R6.Pin_1
  N27: LED3.G, R7.Pin_1

custom parts:
  7-SEGMENT-4DIGIT-YOUNGSUN: This is a part for the 4-Digit 7-segment LEDs from Young Sun. Different from the Digikey LEDs, all 16 pins are used. The LONGPADS Variant is used for a test jig, but you may like it because there is more pad to solder to. If you are concerned about routing space, the standard works just fine though.
