# Fritzing sketch HW5_Environment_Logger_Fritz (saved by Fritzing 0.9.3b)
breadboards: 1

parts:
  Part1 = Arduino Uno (Rev3)
  hc-sr1 = hc-sr04
  R1 = Photocell (LDR) [package=THT]
  LED1 = RGB LED (com. cathode, rbg) [package="5 mm [THT]"]
  R2 = Resistor [tolerance=±5% resistance=10k package=THT]
  R3 = Resistor [tolerance=±5% resistance=330 package=THT]
  R4 = Resistor [tolerance=±5% resistance=330 package=THT]
  R5 = Resistor [tolerance=±5% resistance=330 package=THT]

nets:
  N1: Part1.A0, R1.pin_1, R2.Pin_0
  N2: Part1.D9_PWM, hc-sr1.Trig
  N3: Part1.D10_PWM/SS, hc-sr1.Echo
  N4: Part1.D3_PWM, R3.Pin_0
  N5: Part1.D5_PWM, R5.Pin_1
  N6: Part1.D6_PWM, R4.Pin_1
  5V: Part1.5V, hc-sr1.VCC, R1.pin_0
  GND: Part1.GND, hc-sr1.GND, LED1.common_cathode, R2.Pin_1
  N7: LED1.red_anode, R3.Pin_1
  N8: LED1.blue_anode, R4.Pin_0
  N9: LED1.green_anode, R5.Pin_0
