# Fritzing sketch HW6_Matrix_Game_Demo (saved by Fritzing 0.9.3b)
breadboards: 2

parts:
  Part1 = Arduino Uno (Rev3)
  Disp1 = LBT2088AH [part_number=LBT2088AH]
  U1 = MAX7219 [package=dil24]
  C1 = Capacitor [package=cap-pth-small-kit]
  C2 = Electrolytic Capacitor [capacitance=10µF package="1010 [SMD, electrolytic]"]
  R1 = Resistor [tolerance=±5% resistance=47k package=THT]
  Part2 = Thumb Joystick
  Part3 = Thumb Joystick
  J1 = Piezo Speaker
  R2 = Resistor [tolerance=±5% resistance=100 package=THT]

nets:
  N1: Part1.A0, Part2.VERT
  N2: Part1.A1, Part2.HORZ
  N3: Part1.A2, Part3.VERT
  N4: Part1.A3, Part3.HORZ
  N5: Part1.D9_PWM, R2.Pin_0
  N6: Part1.D10_PWM/SS, U1.LOAD
  N7: Part1.D11_PWM/MOSI, U1.CLK
  N8: Part1.D12/MISO, U1.DIN
  N9: Part1.D6_PWM, Part2.SEL
  N10: Part1.D7, Part3.SEL
  VCC: Part1.5V, Part2.VCC, Part3.VCC
  GND: Part1.GND, U1.GND, U1.GND2, C1.2, C2.-, Part2.GND, Part3.GND, J1.pin1
  N11: Disp1.pin1, U1.SEGD
  N12: Disp1.pin2, U1.SEGF
  N13: Disp1.pin_3, U1.DIG1
  N14: Disp1.pin_4, U1.DIG2
  N15: Disp1.pin_5, U1.SEGG
  N16: Disp1.pin_6, U1.DIG4
  N17: Disp1.pin_7, U1.SEGE
  N18: Disp1.pin_8, U1.SEGB
  N19: Disp1.pin_9, U1.DIG7
  N20: Disp1.pin_10, U1.DIG6
  N21: Disp1.pin_11, U1.SEGA
  N22: Disp1.pin_12, U1.DIG0
  N23: Disp1.pin_13, U1.SEGC
  N24: Disp1.pin_14, U1.DIG5
  N25: Disp1.pin_15, U1.DIG3
  N26: Disp1.pin_16, U1.SEGDP
  N27: U1.ISET, R1.Pin_1
  N28: U1.VCC, C1.1, C2.+, R1.Pin_0
  N29: J1.pin2, R2.Pin_1
